# Fritzing sketch plant-watering-device (saved by Fritzing 0.9.3b)
breadboards: 1

parts:
  Raspberry_Pi_1 = Raspberry Pi 3 [part_number=RPI-3-V1.2]
  Q1 = TRANSISTOR_NPN [package=to-92]
  Q2 = TRANSISTOR_NPN [package=to-92]
  R1 = Resistor [tolerance=±5% resistance=330 package="0603 [SMD]"]
  R2 = Resistor [tolerance=±5% resistance=330 package="0603 [SMD]"]
  LED1 = smd LED [color="Green (555nm)" package="1206 [SMD]"]
  R3 = Resistor [tolerance=±5% resistance=330 package="0603 [SMD]"]
  M1 = DC Motor
  C3 = Ceramic Capacitor [capacitance=100nF package="100 mil [THT, multilayer]"]
  D1 = Diode [package=diode-1n4148]
  C1 = Capacitor Polarized [package=cpol-radial-100uf-25v]

nets:
  N1: Raspberry_Pi_1.GPIO13, R3.Pin_1
  N2: Raspberry_Pi_1.GPIO19, R2.Pin_1
  N3: Raspberry_Pi_1.GPIO26, R1.Pin_1
  N4: Raspberry_Pi_1.GND, LED1.cathode, M1.pin_2, C3.0, C1.-
  N5: Raspberry_Pi_1.5V, Q1.C, Q2.C, C3.1, C1.+
  N6: Q1.E, Q2.E, M1.pin_1, D1.A
  N7: Q1.B, R2.Pin_0
  N8: Q2.B, R1.Pin_0
  N9: LED1.anode, R3.Pin_0
